// Digital circuit ALU8bits.dig as structural Verilog
module ALU8bits (
  input  [2:0] Opcode,
  input  [7:0] B,
  input  [7:0] A,
  input  CLOCK,
  input  G,
  output [7:0] RAC,
  output [7:0] RMQ
);

  wire Cout, D0, D1, D2, D3, D4, D5, D6, D7;
  wire [7:0] AC, MQ, N, Q, R, S, SL, SR, X;

  Demultiplexer #(.Selector_Bits(3)) demultiplexer_1 (
    .sel(Opcode), .in(1'b1), .out_0(D0), .out_1(D1), .out_2(D2), .out_3(D3), .out_4(D4), .out_5(D5),
    .out_6(D6), .out_7(D7));
  // shiftleftac8bits shiftleftac8bits_1: pin names not known; wires that end beside it: A, B, Opcode[0], Cout, N, X, SR, SL, S
  registradores8bits registradores8bits_1 (.A(A), .B(B), .clk(CLOCK), .G(G), .AC(AC), .MQ(MQ));
  divisor8bits divisor8bits_1 (.Dividendo(A), .Divisor(B), .R(R), .Q(Q));
  Multiplexer #(.Selector_Bits(3), .Bits(8)) multiplexer_1 (
    .sel(Opcode), .in_0(S), .in_1(S), .in_2(AC), .in_3(R), .in_4(SR), .in_5(SL), .in_6(N), .in_7(X), .out(RAC));
  Multiplexer #(.Selector_Bits(3), .Bits(8)) multiplexer_2 (
    .sel(Opcode), .in_0({8{1'b0}}), .in_1({8{1'b0}}), .in_2(MQ), .in_3(Q), .in_4({8{1'b0}}),
    .in_5({8{1'b0}}), .in_6({8{1'b0}}), .in_7({8{1'b0}}), .out(RMQ));

  // Other names for the same wires on the sheet: CLK = CLOCK; Op[2:0] = Opcode; Op1 = Opcode[0]; Op2 = Opcode[1];
  //   Op3 = Opcode[2]
endmodule
