// Digital circuit divisor.dig as structural Verilog
module divisor (
  input  [7:0] Ain,
  input  [7:0] Bin,
  output [7:0] R,
  output Q
);

  wire [7:0] S;

  // subtrator8bits subtrator8bits_1: pin names not known; wires that end beside it: Ain, Bin, 1'b1, Q, S
  Multiplexer #(.Bits(8)) multiplexer_1 (.sel(Q), .in_0(Ain), .in_1(S), .out(R));

  // Other names for the same wires on the sheet: Cout = Q
endmodule
