// Digital circuit divisor8bits.dig as structural Verilog
module divisor8bits (
  input  [7:0] Dividendo,
  input  [7:0] Divisor,
  output [7:0] R,
  output [7:0] Q
);

  wire [7:1] A2, A3, A4, A5, A6, A7, A8;
  wire [7:7] R0, R1, R2, R3, R4, R5, R6;

  divisor divisor_1 (.Ain({{7{1'b0}}, Dividendo[7]}), .Bin(Divisor), .R({R0[7], A2}), .Q(Q[7]));
  divisor divisor_2 (.Ain({A2, Dividendo[6]}), .Bin(Divisor), .R({R1[7], A3}), .Q(Q[6]));
  divisor divisor_3 (.Ain({A3, Dividendo[5]}), .Bin(Divisor), .R({R2[7], A4}), .Q(Q[5]));
  divisor divisor_4 (.Ain({A4, Dividendo[4]}), .Bin(Divisor), .R({R3[7], A5}), .Q(Q[4]));
  divisor divisor_5 (.Ain({A5, Dividendo[3]}), .Bin(Divisor), .R({R4[7], A6}), .Q(Q[3]));
  divisor divisor_6 (.Ain({A6, Dividendo[2]}), .Bin(Divisor), .R({R5[7], A7}), .Q(Q[2]));
  divisor divisor_7 (.Ain({A7, Dividendo[1]}), .Bin(Divisor), .R({R6[7], A8}), .Q(Q[1]));
  divisor divisor_8 (.Ain({A8, Dividendo[0]}), .Bin(Divisor), .R(R), .Q(Q[0]));

  // Other names for the same wires on the sheet: A8[0] = Dividendo[0]; D[7:0] = Dividendo; D1 = Dividendo[0];
  //   A7[0] = Dividendo[1]; D2 = Dividendo[1]; A6[0] = Dividendo[2]; D3 = Dividendo[2]; A5[0] = Dividendo[3];
  //   D4 = Dividendo[3]; A4[0] = Dividendo[4]; D5 = Dividendo[4]; A3[0] = Dividendo[5]; D6 = Dividendo[5];
  //   A2[0] = Dividendo[6]; D7 = Dividendo[6]; A1[0] = Dividendo[7]; D8 = Dividendo[7]; d_t[7:0] = Divisor; Q0 = Q[7];
  //   Q1 = Q[6]; Q2 = Q[5]; Q3 = Q[4]; Q4 = Q[3]; Q5 = Q[2]; Q6 = Q[1]; Q7 = Q[0]; R0[6:0] = A2; r1_t[6:0] = A2;
  //   r2_t = R0[7]; R1[6:0] = A3; r3_t[6:0] = A3; r4_t = R1[7]; R2[6:0] = A4; r5_t[6:0] = A4; r6_t = R2[7];
  //   R3[6:0] = A5; r7_t[6:0] = A5; r8 = R3[7]; R4[6:0] = A6; r9[6:0] = A6; r10 = R4[7]; R5[6:0] = A7; r11[6:0] = A7;
  //   r12 = R5[7]; R6[6:0] = A8; r13[6:0] = A8; r14 = R6[7]; R7[7:0] = R
endmodule
