// Digital circuit multiplicador4bits.dig as structural Verilog
module multiplicador4bits (
  input  [3:0] A,
  input  [3:0] B,
  output [7:0] S
);

  wire Cout1, Cout2, E0, E2, E3, E4, E5, E6, E7, E8, E9;
  wire [3:0] PP2, PP3, PP4;

  assign {E4, E3, E2, S[0]} = A & {4{B[0]}};  // And and_1, 4 bits wide
  assign PP2 = A & {4{B[1]}};  // And and_2, 4 bits wide
  assign PP3 = A & {4{B[2]}};  // And and_3, 4 bits wide
  assign PP4 = A & {4{B[3]}};  // And and_4, 4 bits wide
  somador4bits somador4bits_1 (.A({1'b0, E4, E3, E2}), .B(PP2), .Cin(1'b0), .Cout(Cout1), .S({E7, E6, E5, S[1]}));
  somador4bits somador4bits_2 (.A({Cout1, E7, E6, E5}), .B(PP3), .Cin(1'b0), .Cout(Cout2), .S({E0, E9, E8, S[2]}));
  somador4bits somador4bits_3 (.A({Cout2, E0, E9, E8}), .B(PP4), .Cin(1'b0), .Cout(S[7]), .S(S[6:3]));

  // Other names for the same wires on the sheet: B1 = B[0]; BR1[3:0] = {4{B[0]}}; B2 = B[1]; BR2[3:0] = {4{B[1]}};
  //   B3 = B[2]; BR3[3:0] = {4{B[2]}}; B4 = B[3]; BR4[3:0] = {4{B[3]}}; P2[3:0] = {Cout1, E7, E6, E5};
  //   P3[3:0] = {Cout2, E0, E9, E8}; Cout3 = S[7]; PP1[3:0] = {E4, E3, E2, S[0]}; R1 = S[0]; P1[2:0] = {E4, E3, E2};
  //   R2 = S[1]; S1[3:0] = {E7, E6, E5, S[1]}; R3 = S[2]; S2[3:0] = {E0, E9, E8, S[2]}; R4 = S[3]; S3[3:0] = S[6:3];
  //   R5 = S[4]; R6 = S[5]; R7 = S[6]
endmodule
