// Digital circuit multiplicador8bits-v1.dig as structural Verilog
module multiplicador8bits_v1 (
  input  [7:0] A,
  input  [7:0] B,
  input  clk
);

  wire C, D, E;
  wire [3:0] A1, A2, M1, M2;
  wire [7:0] N, S;

  Button u_C (.out(C));
  Button u_D (.out(D));
  Button u_E (.out(E));
  // registrador8bits N: pin names not known; wires that end beside it: C, A, clk, 1'b0, N
  // registrador8bits AC: pin names not known; wires that end beside it: D, S, clk, 1'b0, {A2, A1}
  // registrador8bits MQ: pin names not known; wires that end beside it: E, B, clk, A1[0], {M2, M1}
  somador8bits somador8bits_1 (.A(N), .B({A2, A1}), .Cin(1'b0), .S(S));  // open: Cout
  Seven_Seg_Hex seven_seg_hex_1 (.d(A2), .dp(1'b0));
  Seven_Seg_Hex seven_seg_hex_2 (.d(A1), .dp(1'b0));
  Seven_Seg_Hex seven_seg_hex_3 (.d(M2), .dp(1'b0));
  Seven_Seg_Hex seven_seg_hex_4 (.d(M1), .dp(1'b0));

  // Other names for the same wires on the sheet: AC[7:0] = {A2, A1}; Q1 = A1[0]; Q2 = A1[1]; Q3 = A1[2]; Q4 = A1[3];
  //   Q5 = A2[0]; Q6 = A2[1]; Q7 = A2[2]; Q8 = A2[3]; MQ[7:0] = {M2, M1}
endmodule
