// Digital circuit multiplicador8bits-v2.dig as structural Verilog
module multiplicador8bits_v2 (
  input  [7:0] A,
  input  [7:0] B,
  output [15:0] R
);

  wire C1, C2, C3, C4, C5, C6;
  wire [6:0] F1, F2, F3, F4, F5, F6, F7;
  wire [7:0] PP2, PP3, PP4, PP5, PP6, PP7, PP8;

  assign {F1, R[0]} = A & {8{B[0]}};  // And and_1, 8 bits wide
  assign PP2 = A & {8{B[1]}};  // And and_2, 8 bits wide
  assign PP3 = A & {8{B[2]}};  // And and_3, 8 bits wide
  assign PP4 = A & {8{B[3]}};  // And and_4, 8 bits wide
  assign PP5 = A & {8{B[4]}};  // And and_5, 8 bits wide
  assign PP6 = A & {8{B[5]}};  // And and_6, 8 bits wide
  assign PP7 = A & {8{B[6]}};  // And and_7, 8 bits wide
  assign PP8 = A & {8{B[7]}};  // And and_8, 8 bits wide
  somador8bits somador8bits_1 (.A({1'b0, F1}), .B(PP2), .Cin(1'b0), .Cout(C1), .S({F2, R[1]}));
  somador8bits somador8bits_2 (.A({C1, F2}), .B(PP3), .Cin(1'b0), .Cout(C2), .S({F3, R[2]}));
  somador8bits somador8bits_3 (.A({C2, F3}), .B(PP4), .Cin(1'b0), .Cout(C3), .S({F4, R[3]}));
  somador8bits somador8bits_4 (.A({C3, F4}), .B(PP5), .Cin(1'b0), .Cout(C4), .S({F5, R[4]}));
  somador8bits somador8bits_5 (.A({C4, F5}), .B(PP6), .Cin(1'b0), .Cout(C5), .S({F6, R[5]}));
  somador8bits somador8bits_6 (.A({C5, F6}), .B(PP7), .Cin(1'b0), .Cout(C6), .S({F7, R[6]}));
  somador8bits somador8bits_7 (.A({C6, F7}), .B(PP8), .Cin(1'b0), .Cout(R[15]), .S(R[14:7]));

  // Other names for the same wires on the sheet: B1 = B[0]; BR1[7:0] = {8{B[0]}}; B2 = B[1]; BR2[7:0] = {8{B[1]}};
  //   B3 = B[2]; BR3[7:0] = {8{B[2]}}; B4 = B[3]; BR4[7:0] = {8{B[3]}}; B5 = B[4]; BR5[7:0] = {8{B[4]}}; B6 = B[5];
  //   BR6[7:0] = {8{B[5]}}; B7 = B[6]; BR7[7:0] = {8{B[6]}}; B8 = B[7]; BR8[7:0] = {8{B[7]}}; P2[7:0] = {C1, F2};
  //   P3[7:0] = {C2, F3}; P4[7:0] = {C3, F4}; P5[7:0] = {C4, F5}; P6[7:0] = {C5, F6}; P7[7:0] = {C6, F7}; C7 = R[15];
  //   PP1[7:0] = {F1, R[0]}; R1 = R[0]; P1[6:0] = F1; R2 = R[1]; S1[7:0] = {F2, R[1]}; R3 = R[2];
  //   S2[7:0] = {F3, R[2]}; R4 = R[3]; S3[7:0] = {F4, R[3]}; R5 = R[4]; S4[7:0] = {F5, R[4]}; R6 = R[5];
  //   S5[7:0] = {F6, R[5]}; R7 = R[6]; S6[7:0] = {F7, R[6]}; S7[7:0] = R[14:7]
endmodule
