// Digital circuit registrador8bits.dig as structural Verilog
module registrador8bits (
  input  Load,
  input  [7:0] Din,
  input  CLOCK,
  output [7:0] Dout
);

  wire multiplexer_1_out, multiplexer_2_out, multiplexer_3_out, multiplexer_4_out, multiplexer_5_out,
       multiplexer_6_out, multiplexer_7_out, multiplexer_8_out;

  Multiplexer multiplexer_1 (.sel(Load), .in_0(Dout[0]), .in_1(Din[0]), .out(multiplexer_1_out));
  D_FF d_ff_1 (.D(multiplexer_1_out), .C(CLOCK), .Q(Dout[0]));  // open: nQ
  Multiplexer multiplexer_2 (.sel(Load), .in_0(Dout[1]), .in_1(Din[1]), .out(multiplexer_2_out));
  D_FF d_ff_2 (.D(multiplexer_2_out), .C(CLOCK), .Q(Dout[1]));  // open: nQ
  Multiplexer multiplexer_3 (.sel(Load), .in_0(Dout[2]), .in_1(Din[2]), .out(multiplexer_3_out));
  D_FF d_ff_3 (.D(multiplexer_3_out), .C(CLOCK), .Q(Dout[2]));  // open: nQ
  Multiplexer multiplexer_4 (.sel(Load), .in_0(Dout[3]), .in_1(Din[3]), .out(multiplexer_4_out));
  D_FF d_ff_4 (.D(multiplexer_4_out), .C(CLOCK), .Q(Dout[3]));  // open: nQ
  Multiplexer multiplexer_5 (.sel(Load), .in_0(Dout[4]), .in_1(Din[4]), .out(multiplexer_5_out));
  D_FF d_ff_5 (.D(multiplexer_5_out), .C(CLOCK), .Q(Dout[4]));  // open: nQ
  Multiplexer multiplexer_6 (.sel(Load), .in_0(Dout[5]), .in_1(Din[5]), .out(multiplexer_6_out));
  D_FF d_ff_6 (.D(multiplexer_6_out), .C(CLOCK), .Q(Dout[5]));  // open: nQ
  Multiplexer multiplexer_7 (.sel(Load), .in_0(Dout[6]), .in_1(Din[6]), .out(multiplexer_7_out));
  D_FF d_ff_7 (.D(multiplexer_7_out), .C(CLOCK), .Q(Dout[6]));  // open: nQ
  Multiplexer multiplexer_8 (.sel(Load), .in_0(Dout[7]), .in_1(Din[7]), .out(multiplexer_8_out));
  D_FF d_ff_8 (.D(multiplexer_8_out), .C(CLOCK), .Q(Dout[7]));  // open: nQ

  // Other names for the same wires on the sheet: CLK = CLOCK; D1 = Din[0]; D2 = Din[1]; D3 = Din[2]; D4 = Din[3];
  //   D5 = Din[4]; D6 = Din[5]; D7 = Din[6]; D8 = Din[7]; L = Load; Q1 = Dout[0]; Q2 = Dout[1]; Q3 = Dout[2];
  //   Q4 = Dout[3]; Q5 = Dout[4]; Q6 = Dout[5]; Q7 = Dout[6]; Q8 = Dout[7]
endmodule
