// Digital circuit registradores8bits.dig as structural Verilog
module registradores8bits (
  input  [7:0] A,
  input  [7:0] B,
  input  clk,
  input  G,
  output [7:0] AC,
  output [7:0] MQ
);

  wire [15:0] R;

  multiplicador8bits_v2 multiplicador8bits_v2_1 (.A(A), .B(B), .R(R));
  registrador8bits u_AC (.Load(G), .Din(R[15:8]), .CLOCK(clk), .Dout(AC));
  registrador8bits u_MQ (.Load(G), .Din(R[7:0]), .CLOCK(clk), .Dout(MQ));

  // Other names for the same wires on the sheet: R1[7:0] = R[7:0]; R2[7:0] = R[15:8]
endmodule
