// Digital circuit shiftleftac8bits.dig as structural Verilog
module shiftleftac8bits (
  input  [7:0] A,
  input  [7:0] B,
  input  Op,
  output Cout,
  output [7:0] NAND8BITS,
  output [7:0] XOR8BITS,
  output [7:0] SHIFTRIGHT,
  output [7:0] SHIFTLEFT
);

  wire C1;
  wire [3:0] BL, BM, S1, S2;
  wire [7:0] R;

  assign NAND8BITS = ~(A & B);  // NAnd nand_1, 8 bits wide
  assign XOR8BITS = A ^ B;  // XOr xor_1, 8 bits wide
  Multiplexer #(.Bits(8)) multiplexer_1 (.sel(Op), .in_0(B), .in_1(R), .out({BM, BL}));
  assign R = ~B;  // Not not_1, 8 bits wide
  somador4bits somador4bits_1 (.A(A[3:0]), .B(BL), .Cin(Op), .Cout(C1), .S(S1));
  somador4bits somador4bits_2 (.A(A[7:4]), .B(BM), .Cin(C1), .Cout(Cout), .S(S2));
  Seven_Seg_Hex seven_seg_hex_1 (.d(S2), .dp(1'b0));
  Seven_Seg_Hex seven_seg_hex_2 (.d(S1), .dp(1'b0));

  assign SHIFTLEFT = {A[6:0], 1'b0};
  assign SHIFTRIGHT = {1'b0, A[7:1]};

  // Other names for the same wires on the sheet: A1 = A[0]; A3[6:0] = A[6:0]; AC[7:0] = A; AL[3:0] = A[3:0];
  //   SL[7:1] = A[6:0]; A2[6:0] = A[7:1]; SR[6:0] = A[7:1]; AM[3:0] = A[7:4]; A4 = A[7]; N[7:0] = B;
  //   RN[7:0] = NAND8BITS; RX[7:0] = XOR8BITS
endmodule
