// Digital circuit somador1bit.dig as structural Verilog
module somador1bit (
  input  A,
  input  B,
  input  Cin,
  output Cout,
  output S
);

  wire and_1_out, and_2_out, xor_2_out;

  xor xor_1 (S, A, B, Cin);
  xor xor_2 (xor_2_out, A, B);
  and and_1 (and_1_out, Cin, xor_2_out);
  and and_2 (and_2_out, A, B);
  or or_1 (Cout, and_1_out, and_2_out);
endmodule
