// Digital circuit somador4bits.dig as structural Verilog
module somador4bits (
  input  [3:0] A,
  input  [3:0] B,
  input  Cin,
  output Cout,
  output [3:0] S
);

  wire C1, C2, C3;

  somador1bit somador1bit_1 (.A(A[0]), .B(B[0]), .Cin(Cin), .Cout(C1), .S(S[0]));
  somador1bit somador1bit_2 (.A(A[1]), .B(B[1]), .Cin(C1), .Cout(C2), .S(S[1]));
  somador1bit somador1bit_3 (.A(A[2]), .B(B[2]), .Cin(C2), .Cout(C3), .S(S[2]));
  somador1bit somador1bit_4 (.A(A[3]), .B(B[3]), .Cin(C3), .Cout(Cout), .S(S[3]));
  Seven_Seg_Hex seven_seg_hex_1 (.d(S), .dp(1'b0));

  // Other names for the same wires on the sheet: A2 = A[1]; A4 = A[2]; A8 = A[3]; B2 = B[1]; B4 = B[2]; B8 = B[3];
  //   S1 = S[0]; S2 = S[1]; S3 = S[2]; S4 = S[3]
endmodule
