// Digital circuit somador8bits.dig as structural Verilog
module somador8bits (
  input  [7:0] A,
  input  [7:0] B,
  input  Cin,
  output Cout,
  output [7:0] S
);

  wire C1;

  somador4bits somador4bits_1 (.A(A[3:0]), .B(B[3:0]), .Cin(Cin), .Cout(C1), .S(S[3:0]));
  somador4bits somador4bits_2 (.A(A[7:4]), .B(B[7:4]), .Cin(C1), .Cout(Cout), .S(S[7:4]));
  Seven_Seg_Hex seven_seg_hex_1 (.d(S[7:4]), .dp(1'b0));
  Seven_Seg_Hex seven_seg_hex_2 (.d(S[3:0]), .dp(1'b0));

  // Other names for the same wires on the sheet: AL[3:0] = A[3:0]; AM[3:0] = A[7:4]; BL[3:0] = B[3:0];
  //   BM[3:0] = B[7:4]; S1[3:0] = S[3:0]; S2[3:0] = S[7:4]
endmodule
