// Digital circuit subtrator8bits.dig as structural Verilog
module subtrator8bits (
  input  [7:0] A,
  input  [7:0] B,
  input  Op,
  output Cout
);

  wire C1;
  wire [3:0] BL, BM, S1, S2;
  wire [7:0] R;

  Multiplexer #(.Bits(8)) multiplexer_1 (.sel(Op), .in_0(B), .in_1(R), .out({BM, BL}));
  assign R = ~B;  // Not not_1, 8 bits wide
  somador4bits somador4bits_1 (.A(A[3:0]), .B(BL), .Cin(Op), .Cout(C1), .S(S1));
  somador4bits somador4bits_2 (.A(A[7:4]), .B(BM), .Cin(C1), .Cout(Cout), .S(S2));
  Seven_Seg_Hex seven_seg_hex_1 (.d(S2), .dp(1'b0));
  Seven_Seg_Hex seven_seg_hex_2 (.d(S1), .dp(1'b0));

  // Other names for the same wires on the sheet: AL[3:0] = A[3:0]; AM[3:0] = A[7:4]
endmodule
